// Logisim project MAC.circ as structural Verilog: 9 circuits, main circuit main
module main (
  input  [7:0] DATA,
  input  Man_Clr,
  output [15:0] Saida
);

  wire ADRESS_carry, Clock_out, not_2_out, or_1_out, shift_register_1_out;
  wire [3:0] ADRESS_q, not_1_out;
  wire [7:0] RAM_saida, ROM_saida;

  Counter #(.width(4), .max('hf)) ADRESS (
    .count(1'b1), .Q(ADRESS_q), .carry(ADRESS_carry), .clk(Clock_out), .clr(Man_Clr));  // open: load, D
  assign not_1_out = ~ADRESS_q;  // NOT_Gate not_1, 4 bits wide
  Shift_Register #(.length(1)) shift_register_1 (
    .shift(not_2_out), .in(ADRESS_carry), .clk(not_2_out), .out(shift_register_1_out));  // open: load, clr, d0, q0
  not not_2 (not_2_out, Clock_out);
  // Probe on ADRESS_q
  // Probe on not_1_out
  or or_1 (or_1_out, Man_Clr, shift_register_1_out);
  RAM RAM (.\Endereço (ADRESS_q), .Dados(DATA), .clr(or_1_out), .clk_str_ld(Clock_out), .saida(RAM_saida));
  ROM ROM (.Entrada(not_1_out), .clk(Clock_out), .clr(or_1_out), .Saida(ROM_saida));
  // Probe on RAM_saida
  // Probe on ROM_saida
  MAC MAC (.Entrada_RAM(RAM_saida), .Entrada_ROM(ROM_saida), .Clock(Clock_out), .Clear(or_1_out), .Saida(Saida));
  Clock Clock (.out(Clock_out));
endmodule

module RAM (
  input  [3:0] \Endereço ,
  input  [7:0] Dados,
  input  clr,
  input  clk_str_ld,
  output [7:0] saida
);

  wire not_1_out, not_2_out;
  wire [3:0] shift_register_1_out;
  wire [7:0] ram_1_data;

  not not_1 (not_1_out, clk_str_ld);
  Shift_Register #(.width(4), .length(1)) shift_register_1 (
    .shift(not_1_out), .in(\Endereço ), .clk(not_1_out), .out(shift_register_1_out), .load(1'b0), .clr(clr));  // open: d0, q0
  not not_2 (not_2_out, clk_str_ld);
  RAM_part #(.addrWidth(4), .bus("separate")) ram_1 (
    .addr(shift_register_1_out), .din(Dados), .data(ram_1_data), .str(not_2_out), .sel(1'b1),
    .clk(clk_str_ld), .ld(clk_str_ld), .clr(clr));
  Register #(.trigger("high")) register_1 (.D(ram_1_data), .en(1'b1), .Q(saida), .clk(clk_str_ld), .clr(clr));
endmodule

module ROM (
  input  [3:0] Entrada,
  input  clk,
  input  clr,
  output [7:0] Saida
);

  wire [7:0] rom_1_data;

  ROM_part #(.addrWidth(4)) rom_1 (.addr(Entrada), .data(rom_1_data), .sel(1'b1));
  Shift_Register #(.width(8), .length(1)) shift_register_1 (
    .shift(clk), .in(rom_1_data), .clk(clk), .out(Saida), .clr(clr));  // open: load, d0, q0

  // Notes on the sheet:
  //   contents of rom_1 (hex, n*v repeats v):
  //   86 c6 d6 76 a1 64 8c ab b3 a9 8d 64 86 c6 d6 76
endmodule

module MAC (
  input  [7:0] Entrada_RAM,
  input  [7:0] Entrada_ROM,
  input  Clock,
  input  Clear,
  output [15:0] Saida
);

  wire [7:0] multiplier_1_cout, multiplier_1_out;
  wire [15:0] Reg_q;

  Multiplier multiplier_1 (
    .a(Entrada_RAM), .b(Entrada_ROM), .out(multiplier_1_out), .cout(multiplier_1_cout));  // open: cin
  soma_main soma_main_1 (
    .Entrada_A({multiplier_1_cout, multiplier_1_out}), .Entrada_B(Reg_q), .Sel_A(1'b1), .Sel_B(1'b1),
    .Saida(Saida));  // open: Carry
  Register #(.width(16)) Reg (.D(Saida), .en(1'b1), .Q(Reg_q), .clk(Clock), .clr(Clear));
endmodule

module soma_main (
  input  [15:0] Entrada_A,
  input  Sel_A,
  input  [15:0] Entrada_B,
  input  Sel_B,
  output Carry,
  output [15:0] Saida
);

  wire [15:0] C2A_saida, C2B_saida, multiplexer_1_out, multiplexer_2_out;

  C2 C2A (.ENTRADA(Entrada_A), .SAIDA(C2A_saida));
  C2 C2B (.ENTRADA(Entrada_B), .SAIDA(C2B_saida));
  Multiplexer #(.width(16), .enable("false")) multiplexer_1 (
    .in0(C2A_saida), .in1(Entrada_A), .out(multiplexer_1_out), .sel(Sel_A));
  Multiplexer #(.width(16), .enable("false")) multiplexer_2 (
    .in0(C2B_saida), .in1(Entrada_B), .out(multiplexer_2_out), .sel(Sel_B));
  SOMADOR_16BITS Soma (.Saida(Saida), .Entrada_B(multiplexer_2_out), .Entrada_A(multiplexer_1_out), .Carry(Carry));
endmodule

module HALF_ADDER (
  input  A,
  input  B,
  output CARRY,
  output SAIDA
);

  and and_1 (CARRY, A, B);
  xor xor_1 (SAIDA, A, B);
endmodule

module FULL_ADDER (
  input  A,
  input  B,
  input  Cin,
  output SAIDA,
  output Cout
);

  wire and_1_out, and_2_out, xor_1_out;

  xor xor_1 (xor_1_out, A, B);
  xor xor_2 (SAIDA, xor_1_out, Cin);
  and and_1 (and_1_out, Cin, xor_1_out);
  and and_2 (and_2_out, B, A);
  or or_1 (Cout, and_1_out, and_2_out);
endmodule

module C2 (
  input  [15:0] ENTRADA,
  output [15:0] SAIDA
);

  wire [15:0] not_1_out;

  assign not_1_out = ~ENTRADA;  // NOT_Gate not_1, 16 bits wide
  SOMADOR_16BITS somador_16bits_1 (.Saida(SAIDA), .Entrada_B(16'h1), .Entrada_A(not_1_out));  // open: Carry
endmodule

module SOMADOR_16BITS (
  input  [15:0] Entrada_B,
  input  [15:0] Entrada_A,
  output [15:0] Saida,
  output Carry
);

  wire full_adder_1_cout, full_adder_2_cout, full_adder_3_cout, full_adder_4_cout, full_adder_5_cout,
       full_adder_6_cout, full_adder_7_cout, full_adder_8_cout, full_adder_9_cout, full_adder_10_cout,
       full_adder_11_cout, full_adder_12_cout, full_adder_13_cout, full_adder_14_cout, half_adder_1_carry;

  HALF_ADDER half_adder_1 (.A(Entrada_A[0]), .B(Entrada_B[0]), .CARRY(half_adder_1_carry), .SAIDA(Saida[0]));
  FULL_ADDER full_adder_1 (
    .A(Entrada_A[1]), .B(Entrada_B[1]), .Cin(half_adder_1_carry), .SAIDA(Saida[1]), .Cout(full_adder_1_cout));
  FULL_ADDER full_adder_2 (
    .A(Entrada_A[2]), .B(Entrada_B[2]), .Cin(full_adder_1_cout), .SAIDA(Saida[2]), .Cout(full_adder_2_cout));
  FULL_ADDER full_adder_3 (
    .A(Entrada_A[3]), .B(Entrada_B[3]), .Cin(full_adder_2_cout), .SAIDA(Saida[3]), .Cout(full_adder_3_cout));
  FULL_ADDER full_adder_4 (
    .A(Entrada_A[4]), .B(Entrada_B[4]), .Cin(full_adder_3_cout), .SAIDA(Saida[4]), .Cout(full_adder_4_cout));
  FULL_ADDER full_adder_5 (
    .A(Entrada_A[5]), .B(Entrada_B[5]), .Cin(full_adder_4_cout), .SAIDA(Saida[5]), .Cout(full_adder_5_cout));
  FULL_ADDER full_adder_6 (
    .A(Entrada_A[6]), .B(Entrada_B[6]), .Cin(full_adder_5_cout), .SAIDA(Saida[6]), .Cout(full_adder_6_cout));
  FULL_ADDER full_adder_7 (
    .A(Entrada_A[7]), .B(Entrada_B[7]), .Cin(full_adder_6_cout), .SAIDA(Saida[7]), .Cout(full_adder_7_cout));
  FULL_ADDER full_adder_8 (
    .A(Entrada_A[9]), .B(Entrada_B[9]), .Cin(full_adder_9_cout), .SAIDA(Saida[9]), .Cout(full_adder_8_cout));
  FULL_ADDER full_adder_9 (
    .A(Entrada_A[8]), .B(Entrada_B[8]), .Cin(full_adder_7_cout), .SAIDA(Saida[8]), .Cout(full_adder_9_cout));
  FULL_ADDER full_adder_10 (
    .A(Entrada_A[10]), .B(Entrada_B[10]), .Cin(full_adder_8_cout), .SAIDA(Saida[10]),
    .Cout(full_adder_10_cout));
  FULL_ADDER full_adder_11 (
    .A(Entrada_A[11]), .B(Entrada_B[11]), .Cin(full_adder_10_cout), .SAIDA(Saida[11]),
    .Cout(full_adder_11_cout));
  FULL_ADDER full_adder_12 (
    .A(Entrada_A[12]), .B(Entrada_B[12]), .Cin(full_adder_11_cout), .SAIDA(Saida[12]),
    .Cout(full_adder_12_cout));
  FULL_ADDER full_adder_13 (
    .A(Entrada_A[13]), .B(Entrada_B[13]), .Cin(full_adder_12_cout), .SAIDA(Saida[13]),
    .Cout(full_adder_13_cout));
  FULL_ADDER full_adder_14 (
    .A(Entrada_A[14]), .B(Entrada_B[14]), .Cin(full_adder_13_cout), .SAIDA(Saida[14]),
    .Cout(full_adder_14_cout));
  FULL_ADDER full_adder_15 (
    .A(Entrada_A[15]), .B(Entrada_B[15]), .Cin(full_adder_14_cout), .SAIDA(Saida[15]), .Cout(Carry));
endmodule
