// Logisim project MIPS_L-Parte 1.circ as structural Verilog: 15 circuits, main circuit main
// CAM_DADOS
module main (
  input  CLR
);

  wire cam_controle_1_en_ram, cam_controle_1_read_ram, cam_controle_1_sel_op2, cam_controle_1_sel_ula,
       cam_controle_1_wr_acc, cam_controle_1_wr_ram, CLK_out;
  wire [1:0] cam_controle_1_sel_op1;
  wire [5:0] cam_dados_1_bits___signf;
  wire [25:0] cam_controle_1_mem_prog, cam_dados_1_add_ram;
  wire [31:0] cam_dados_1_din_ram, ram_1_dout, rom_1_saida;

  Clock CLK (.out(CLK_out));
  CAM_DADOS cam_dados_1 (
    .Dout_ROM(rom_1_saida), .CLK(CLK_out), .Dout_RAM(ram_1_dout), .Bits___Signf(cam_dados_1_bits___signf),
    .ADD_RAM(cam_dados_1_add_ram), .SEL_OP2(cam_controle_1_sel_op2), .SEL_OP1(cam_controle_1_sel_op1),
    .WR_ACC(cam_controle_1_wr_acc), .CLR_ACC_IR(CLR), .DIN_RAM(cam_dados_1_din_ram),
    .SEL_ULA(cam_controle_1_sel_ula));
  ROM rom_1 (.ENTRADA(cam_controle_1_mem_prog), .SAIDA(rom_1_saida));
  RAM ram_1 (
    .ADD_RAM(cam_dados_1_add_ram), .DIN_RAM(cam_dados_1_din_ram), .WR_RAM(cam_controle_1_wr_ram),
    .EN_RAM(cam_controle_1_en_ram), .CLK(CLK_out), .RD_RAM(cam_controle_1_read_ram), .CLR(CLR),
    .DOUT(ram_1_dout));
  CAM_CONTROLE cam_controle_1 (
    .BITS___SIGNF(cam_dados_1_bits___signf), .CLR_PC(CLR), .CLK(CLK_out), .MEM_PROG(cam_controle_1_mem_prog),
    .EN_RAM(cam_controle_1_en_ram), .WR_RAM(cam_controle_1_wr_ram), .READ_RAM(cam_controle_1_read_ram),
    .WR_ACC(cam_controle_1_wr_acc), .SEL_OP1(cam_controle_1_sel_op1), .SEL_OP2(cam_controle_1_sel_op2),
    .SEL_ULA(cam_controle_1_sel_ula));
  // Probe on rom_1_saida
  // Probe on cam_dados_1_bits___signf
endmodule

module ULA (
  input  [31:0] ACC,
  input  [31:0] MUX,
  input  SEL_ULA,
  output [31:0] SAIDA
);

  wire [31:0] adder_1_out, subtractor_1_out;

  Adder #(.width(32)) adder_1 (.a(ACC), .b(MUX), .out(adder_1_out));  // open: cin, cout
  Subtractor #(.width(32)) subtractor_1 (.a(ACC), .b(MUX), .out(subtractor_1_out));  // open: bin, bout
  Multiplexer #(.width(32)) multiplexer_1 (
    .in0(adder_1_out), .in1(subtractor_1_out), .out(SAIDA), .sel(SEL_ULA), .en(1'b1));
endmodule

module RAM (
  input  [25:0] ADD_RAM,
  input  [31:0] DIN_RAM,
  input  WR_RAM,
  input  EN_RAM,
  input  RD_RAM,
  input  CLR,
  input  CLK,
  output [31:0] DOUT
);

  RAM_part #(.addrWidth(24), .dataWidth(32), .bus("separate")) ram_1 (
    .addr(ADD_RAM[23:0]), .din(DIN_RAM), .data(DOUT), .str(WR_RAM), .sel(EN_RAM), .clk(CLK), .ld(RD_RAM),
    .clr(CLR));
  // also tied to GND on the sheet: {ADD_RAM[24], ADD_RAM[25]}
endmodule

module PC (
  input  EN_PC,
  input  CLR_PC,
  input  CLK,
  output [25:0] MEM_PROG
);

  wire [25:0] adder_1_out;

  Register #(.width(26)) PC (.D(adder_1_out), .en(EN_PC), .Q(MEM_PROG), .clk(CLK), .clr(CLR_PC));
  Adder #(.width(26)) adder_1 (.a(MEM_PROG), .b(26'h1), .out(adder_1_out));  // open: cin, cout
endmodule

module ROM (
  input  [25:0] ENTRADA,
  output [31:0] SAIDA
);

  ROM_part #(.addrWidth(24), .dataWidth(32)) rom_1 (.addr(ENTRADA[23:0]), .data(SAIDA), .sel(1'b1));
  // also tied to GND on the sheet: {ENTRADA[24], ENTRADA[25]}

  // Notes on the sheet:
  //   contents of rom_1 (hex, n*v repeats v):
  //   c000005 4000000 c000003 4000001 10000000 4000002 18000001 14000006 1c000003 4000004 8000002 18000004
endmodule

// CONTROLE
module CAM_CONTROLE (
  input  [5:0] BITS___SIGNF,
  input  CLR_PC,
  input  CLK,
  output EN_RAM,
  output WR_RAM,
  output READ_RAM,
  output WR_ACC,
  output [1:0] SEL_OP1,
  output [25:0] MEM_PROG,
  output SEL_OP2,
  output SEL_ULA
);

  wire en_pc_1_en_pc;

  EN_RAM en_ram_1 (.BITS___SIGNF(BITS___SIGNF), .EN_RAM(EN_RAM));
  WR_RAM wr_ram_1 (.BITS___SIGNF(BITS___SIGNF), .WR_RAM(WR_RAM));
  READ_RAM read_ram_1 (.BITS___SIGNF(BITS___SIGNF), .READ_RAM(READ_RAM));
  EN_PC en_pc_1 (.BITS___SIGNF(BITS___SIGNF), .EN_PC(en_pc_1_en_pc));
  WR_ACC wr_acc_1 (.BITS___SIGNF(BITS___SIGNF), .WR_ACC(WR_ACC));
  SEL_OP1 sel_op1_1 (.BITS___SIGNF(BITS___SIGNF), .SEL_OP1(SEL_OP1));
  SEL_OP2 sel_op2_1 (.BITS___SIGNF(BITS___SIGNF), .SEL_OP2(SEL_OP2));
  SEL_ULA sel_ula_1 (.BITS___SIGNF(BITS___SIGNF), .SEL_ULA(SEL_ULA));
  PC pc_1 (.EN_PC(en_pc_1_en_pc), .CLR_PC(CLR_PC), .CLK(CLK), .MEM_PROG(MEM_PROG));
endmodule

module EN_RAM (
  input  [5:0] BITS___SIGNF,
  output EN_RAM
);

  wire and_1_out, and_2_out, and_3_out, not_1_out, not_2_out, not_3_out, not_4_out, or_1_out;

  not not_1 (not_1_out, BITS___SIGNF[0]);
  not not_2 (not_2_out, BITS___SIGNF[0]);
  not not_3 (not_3_out, BITS___SIGNF[1]);
  not not_4 (not_4_out, BITS___SIGNF[2]);
  and and_1 (and_1_out, BITS___SIGNF[1], not_1_out);
  and and_2 (and_2_out, BITS___SIGNF[2], not_2_out);
  and and_3 (and_3_out, BITS___SIGNF[0], not_3_out, not_4_out);
  or or_1 (or_1_out, and_1_out, and_2_out);
  or or_2 (EN_RAM, or_1_out, and_3_out);
  // also tied to GND on the sheet: {BITS___SIGNF[3], BITS___SIGNF[4], BITS___SIGNF[5]}
endmodule

module CAM_DADOS (
  input  [31:0] Dout_ROM,
  input  [1:0] SEL_OP1,
  input  WR_ACC,
  input  SEL_ULA,
  input  CLK,
  input  CLR_ACC_IR,
  input  [31:0] Dout_RAM,
  input  SEL_OP2,
  output [5:0] Bits___Signf,
  output [31:0] DIN_RAM,
  output [25:0] ADD_RAM
);

  wire [31:0] bit_extender_1_out, multiplexer_1_out, multiplexer_2_out, ula_1_saida;

  Register #(.width(32)) IR (.D(Dout_ROM), .en(1'b1), .Q({Bits___Signf, ADD_RAM}), .clk(CLK), .clr(CLR_ACC_IR));
  assign bit_extender_1_out = {{6{1'b0}}, ADD_RAM};  // Bit_Extender bit_extender_1
  Multiplexer #(.width(32)) multiplexer_1 (
    .in0(bit_extender_1_out), .in1(Dout_RAM), .out(multiplexer_1_out), .sel(SEL_OP2), .en(1'b1));
  Multiplexer #(.select(2), .width(32)) multiplexer_2 (
    .in0(ula_1_saida), .in1(bit_extender_1_out), .in2(Dout_RAM), .in3({32{1'b0}}), .out(multiplexer_2_out),
    .sel(SEL_OP1), .en(1'b1));
  Register #(.width(32)) ACC (.D(multiplexer_2_out), .en(WR_ACC), .Q(DIN_RAM), .clk(CLK), .clr(CLR_ACC_IR));
  ULA ula_1 (.ACC(DIN_RAM), .MUX(multiplexer_1_out), .SEL_ULA(SEL_ULA), .SAIDA(ula_1_saida));
endmodule

module WR_RAM (
  input  [5:0] BITS___SIGNF,
  output WR_RAM
);

  wire not_1_out, not_2_out;

  not not_1 (not_1_out, BITS___SIGNF[2]);
  not not_2 (not_2_out, BITS___SIGNF[1]);
  and and_1 (WR_RAM, not_1_out, not_2_out, BITS___SIGNF[0]);
  // also tied to GND on the sheet: {BITS___SIGNF[3], BITS___SIGNF[4], BITS___SIGNF[5]}
endmodule

module READ_RAM (
  input  [5:0] BITS___SIGNF,
  output READ_RAM
);

  wire and_1_out, and_2_out, not_1_out, not_2_out;

  not not_1 (not_1_out, BITS___SIGNF[0]);
  not not_2 (not_2_out, BITS___SIGNF[0]);
  and and_1 (and_1_out, BITS___SIGNF[1], not_1_out);
  and and_2 (and_2_out, BITS___SIGNF[2], not_2_out);
  or or_1 (READ_RAM, and_1_out, and_2_out);
  // also tied to GND on the sheet: {BITS___SIGNF[3], BITS___SIGNF[4], BITS___SIGNF[5]}
endmodule

module EN_PC (
  input  [5:0] BITS___SIGNF,
  output EN_PC
);

  wire or_1_out;

  or or_1 (or_1_out, BITS___SIGNF[0], BITS___SIGNF[1]);
  or or_2 (EN_PC, or_1_out, BITS___SIGNF[2]);
  // also tied to GND on the sheet: {BITS___SIGNF[3], BITS___SIGNF[4], BITS___SIGNF[5]}
endmodule

module WR_ACC (
  input  [5:0] BITS___SIGNF,
  output WR_ACC
);

  or or_1 (WR_ACC, BITS___SIGNF[1], BITS___SIGNF[2]);
  // also tied to GND on the sheet: {BITS___SIGNF[3], BITS___SIGNF[4], BITS___SIGNF[5]}
endmodule

module SEL_OP1 (
  input  [5:0] BITS___SIGNF,
  output [1:0] SEL_OP1
);

  wire not_1_out, not_2_out, not_3_out;

  not not_1 (not_1_out, BITS___SIGNF[2]);
  not not_2 (not_2_out, BITS___SIGNF[0]);
  not not_3 (not_3_out, BITS___SIGNF[2]);
  and and_1 (SEL_OP1[1], not_1_out, BITS___SIGNF[1], not_2_out);
  and and_2 (SEL_OP1[0], not_3_out, BITS___SIGNF[1], BITS___SIGNF[0]);
  // also tied to GND on the sheet: {BITS___SIGNF[3], BITS___SIGNF[4], BITS___SIGNF[5]}
endmodule

module SEL_OP2 (
  input  [5:0] BITS___SIGNF,
  output SEL_OP2
);

  wire not_1_out;

  not not_1 (not_1_out, BITS___SIGNF[0]);
  and and_1 (SEL_OP2, BITS___SIGNF[2], not_1_out);
  // also tied to GND on the sheet: {BITS___SIGNF[3], BITS___SIGNF[4], BITS___SIGNF[5]}
endmodule

module SEL_ULA (
  input  [5:0] BITS___SIGNF,
  output SEL_ULA
);

  and and_1 (SEL_ULA, BITS___SIGNF[1], BITS___SIGNF[2]);
  // also tied to GND on the sheet: {BITS___SIGNF[3], BITS___SIGNF[4], BITS___SIGNF[5]}
endmodule
