// Logisim project MIPS_L-Parte2.circ as structural Verilog: 17 circuits, main circuit main
// CAM_DADOS
module main (
  input  CLR
);

  wire cam_controle_1_en_mon, cam_controle_1_en_ram, cam_controle_1_en_tec, cam_controle_1_read_ram,
       cam_controle_1_sel_op2, cam_controle_1_sel_ula, cam_controle_1_wr_acc, cam_controle_1_wr_ram, CLK_out;
  wire [1:0] cam_controle_1_sel_op1;
  wire [5:0] cam_dados_1_bits___signf;
  wire [6:0] keyboard_1_data;
  wire [25:0] cam_controle_1_mem_prog, cam_dados_1_add_imed;
  wire [31:0] cam_dados_1_din_bus, ram_1_dout_bus, rom_1_saida;

  Clock CLK (.out(CLK_out));
  CAM_DADOS cam_dados_1 (
    .Dout_ROM(rom_1_saida), .CLK(CLK_out), .Dout_BUS(ram_1_dout_bus),
    .Bits___Signf(cam_dados_1_bits___signf), .DOUT_TEC(keyboard_1_data), .ADD_IMED(cam_dados_1_add_imed),
    .SEL_OP2(cam_controle_1_sel_op2), .SEL_OP1(cam_controle_1_sel_op1), .WR_ACC(cam_controle_1_wr_acc),
    .CLR_ACC_IR(CLR), .DIN_BUS(cam_dados_1_din_bus), .SEL_ULA(cam_controle_1_sel_ula));
  Keyboard keyboard_1 (.clk(CLK_out), .re(cam_controle_1_en_tec), .clr(CLR), .data(keyboard_1_data));  // open: avail
  ROM rom_1 (.ENTRADA(cam_controle_1_mem_prog), .SAIDA(rom_1_saida));
  RAM ram_1 (
    .ADD_IMED(cam_dados_1_add_imed), .DIN_BUS(cam_dados_1_din_bus), .WR_RAM(cam_controle_1_wr_ram),
    .EN_RAM(cam_controle_1_en_ram), .CLK(CLK_out), .RD_RAM(cam_controle_1_read_ram), .CLR(CLR),
    .DOUT_BUS(ram_1_dout_bus));
  // Probe on rom_1_saida
  CAM_CONTROLE cam_controle_1 (
    .BITS___SIGNF(cam_dados_1_bits___signf), .CLK(CLK_out), .ADD_IMED(cam_dados_1_add_imed), .CLR_PC(CLR),
    .MEM_PROG(cam_controle_1_mem_prog), .EN_RAM(cam_controle_1_en_ram), .WR_RAM(cam_controle_1_wr_ram),
    .READ_RAM(cam_controle_1_read_ram), .WR_ACC(cam_controle_1_wr_acc), .SEL_OP1(cam_controle_1_sel_op1),
    .SEL_OP2(cam_controle_1_sel_op2), .SEL_ULA(cam_controle_1_sel_ula), .EN_TEC(cam_controle_1_en_tec),
    .EN_MON(cam_controle_1_en_mon));
  TTY tty_1 (.data(cam_dados_1_din_bus[6:0]), .clk(CLK_out), .we(cam_controle_1_en_mon), .clr(CLR));
endmodule

module ULA (
  input  [31:0] ACC,
  input  [31:0] MUX,
  input  SEL_ULA,
  output [31:0] SAIDA
);

  wire [31:0] adder_1_out, subtractor_1_out;

  Adder #(.width(32)) adder_1 (.a(ACC), .b(MUX), .out(adder_1_out));  // open: cin, cout
  Subtractor #(.width(32)) subtractor_1 (.a(ACC), .b(MUX), .out(subtractor_1_out));  // open: bin, bout
  Multiplexer #(.width(32)) multiplexer_1 (
    .in0(adder_1_out), .in1(subtractor_1_out), .out(SAIDA), .sel(SEL_ULA), .en(1'b1));
endmodule

module RAM (
  input  [25:0] ADD_IMED,
  input  [31:0] DIN_BUS,
  input  WR_RAM,
  input  EN_RAM,
  input  RD_RAM,
  input  CLR,
  input  CLK,
  output [31:0] DOUT_BUS
);

  RAM_part #(.addrWidth(24), .dataWidth(32), .bus("separate")) ram_1 (
    .addr(ADD_IMED[23:0]), .din(DIN_BUS), .data(DOUT_BUS), .str(WR_RAM), .sel(EN_RAM), .clk(CLK),
    .ld(RD_RAM), .clr(CLR));
  // also tied to GND on the sheet: {ADD_IMED[24], ADD_IMED[25]}
endmodule

module ROM (
  input  [25:0] ENTRADA,
  output [31:0] SAIDA
);

  ROM_part #(.addrWidth(24), .dataWidth(32)) rom_1 (.addr(ENTRADA[23:0]), .data(SAIDA), .sel(1'b1));
  // also tied to GND on the sheet: {ENTRADA[24], ENTRADA[25]}

  // Notes on the sheet:
  //   contents of rom_1 (hex, n*v repeats v):
  //   24000000 28000000 14000001 20000001
endmodule

// CONTROLE
module CAM_CONTROLE (
  input  [5:0] BITS___SIGNF,
  input  CLK,
  input  CLR_PC,
  input  [25:0] ADD_IMED,
  output EN_RAM,
  output WR_RAM,
  output READ_RAM,
  output WR_ACC,
  output [1:0] SEL_OP1,
  output SEL_OP2,
  output [25:0] MEM_PROG,
  output SEL_ULA,
  output EN_TEC,
  output EN_MON
);

  wire en_pc_1_en_pc, sel_jump_1_sel_jump;
  wire [25:0] adder_1_out, PC_q;

  EN_RAM en_ram_1 (.BITS___SIGNF(BITS___SIGNF), .EN_RAM(EN_RAM));
  WR_RAM wr_ram_1 (.BITS___SIGNF(BITS___SIGNF), .WR_RAM(WR_RAM));
  READ_RAM read_ram_1 (.BITS___SIGNF(BITS___SIGNF), .RD_RAM(READ_RAM));
  EN_PC en_pc_1 (.BITS___SIGNF(BITS___SIGNF), .EN_PC(en_pc_1_en_pc));
  WR_ACC wr_acc_1 (.BITS___SIGNF(BITS___SIGNF), .WR_ACC(WR_ACC));
  SEL_OP1 sel_op1_1 (.BITS___SIGNF(BITS___SIGNF), .SEL_OP1(SEL_OP1));
  SEL_OP2 sel_op2_1 (.BITS___SIGNF(BITS___SIGNF), .SEL_OP2(SEL_OP2));
  SEL_ULA sel_ula_1 (.BITS___SIGNF(BITS___SIGNF), .SEL_ULA(SEL_ULA));
  EN_TEC en_tec_1 (.BITS___SIGNF(BITS___SIGNF), .EN_TEC(EN_TEC));
  EN_MON en_mon_1 (.BITS___SIGNF(BITS___SIGNF), .EN_MON(EN_MON));
  SEL_JUMP sel_jump_1 (.BITS___SIGNF(BITS___SIGNF), .SEL_JUMP(sel_jump_1_sel_jump));
  Register #(.width(26)) PC (.D(adder_1_out), .en(en_pc_1_en_pc), .Q(PC_q), .clk(CLK), .clr(CLR_PC));
  Multiplexer #(.width(26)) multiplexer_1 (
    .in0(PC_q), .in1(ADD_IMED), .out(MEM_PROG), .sel(sel_jump_1_sel_jump), .en(1'b1));
  Adder #(.width(26)) adder_1 (.a(MEM_PROG), .b(26'h1), .out(adder_1_out));  // open: cin, cout
endmodule

module EN_RAM (
  input  [5:0] BITS___SIGNF,
  output EN_RAM
);

  wire and_1_out, and_2_out, and_3_out, not_1_out, not_2_out, not_3_out, not_4_out, not_5_out, not_6_out,
       not_7_out, not_8_out, not_9_out, not_10_out, not_11_out, not_12_out, not_13_out;

  not not_1 (not_1_out, BITS___SIGNF[0]);
  not not_2 (not_2_out, BITS___SIGNF[3]);
  not not_3 (not_3_out, BITS___SIGNF[4]);
  not not_4 (not_4_out, BITS___SIGNF[5]);
  not not_5 (not_5_out, BITS___SIGNF[0]);
  not not_6 (not_6_out, BITS___SIGNF[3]);
  not not_7 (not_7_out, BITS___SIGNF[4]);
  not not_8 (not_8_out, BITS___SIGNF[5]);
  not not_9 (not_9_out, BITS___SIGNF[1]);
  not not_10 (not_10_out, BITS___SIGNF[2]);
  not not_11 (not_11_out, BITS___SIGNF[3]);
  not not_12 (not_12_out, BITS___SIGNF[4]);
  not not_13 (not_13_out, BITS___SIGNF[5]);
  and and_1 (and_1_out, not_1_out, BITS___SIGNF[1], not_2_out, not_3_out, not_4_out);
  and and_2 (and_2_out, not_5_out, BITS___SIGNF[2], not_6_out, not_7_out, not_8_out);
  and and_3 (and_3_out, BITS___SIGNF[0], not_9_out, not_10_out, not_11_out, not_12_out, not_13_out);
  or or_1 (EN_RAM, and_1_out, and_2_out, and_3_out);
endmodule

module CAM_DADOS (
  input  [6:0] DOUT_TEC,
  input  [31:0] Dout_ROM,
  input  [1:0] SEL_OP1,
  input  WR_ACC,
  input  SEL_ULA,
  input  CLK,
  input  CLR_ACC_IR,
  input  [31:0] Dout_BUS,
  input  SEL_OP2,
  output [5:0] Bits___Signf,
  output [31:0] DIN_BUS,
  output [25:0] ADD_IMED
);

  wire [31:0] bit_extender_1_out, bit_extender_2_out, multiplexer_1_out, multiplexer_2_out, ula_1_saida;

  Register #(.width(32)) IR (.D(Dout_ROM), .en(1'b1), .Q({Bits___Signf, ADD_IMED}), .clk(CLK), .clr(CLR_ACC_IR));
  assign bit_extender_1_out = {{6{1'b0}}, ADD_IMED};  // Bit_Extender bit_extender_1
  assign bit_extender_2_out = {{25{1'b0}}, DOUT_TEC};  // Bit_Extender bit_extender_2
  Multiplexer #(.width(32)) multiplexer_1 (
    .in0(bit_extender_1_out), .in1(Dout_BUS), .out(multiplexer_1_out), .sel(SEL_OP2), .en(1'b1));
  Multiplexer #(.select(2), .width(32)) multiplexer_2 (
    .in0(ula_1_saida), .in1(bit_extender_1_out), .in2(bit_extender_2_out), .in3(Dout_BUS),
    .out(multiplexer_2_out), .sel(SEL_OP1), .en(1'b1));
  Register #(.width(32)) ACC (.D(multiplexer_2_out), .en(WR_ACC), .Q(DIN_BUS), .clk(CLK), .clr(CLR_ACC_IR));
  ULA ula_1 (.ACC(DIN_BUS), .MUX(multiplexer_1_out), .SEL_ULA(SEL_ULA), .SAIDA(ula_1_saida));
endmodule

module WR_RAM (
  input  [5:0] BITS___SIGNF,
  output WR_RAM
);

  wire not_1_out, not_2_out, not_3_out, not_4_out, not_5_out;

  not not_1 (not_1_out, BITS___SIGNF[1]);
  not not_2 (not_2_out, BITS___SIGNF[4]);
  not not_3 (not_3_out, BITS___SIGNF[2]);
  not not_4 (not_4_out, BITS___SIGNF[3]);
  not not_5 (not_5_out, BITS___SIGNF[5]);
  and and_1 (WR_RAM, BITS___SIGNF[0], not_1_out, not_3_out, not_4_out, not_2_out, not_5_out);
endmodule

module READ_RAM (
  input  [5:0] BITS___SIGNF,
  output RD_RAM
);

  wire and_1_out, and_2_out, not_1_out, not_2_out, not_3_out, not_4_out, not_5_out, not_6_out, not_7_out,
       not_8_out;

  not not_1 (not_1_out, BITS___SIGNF[0]);
  not not_2 (not_2_out, BITS___SIGNF[4]);
  not not_3 (not_3_out, BITS___SIGNF[0]);
  not not_4 (not_4_out, BITS___SIGNF[3]);
  not not_5 (not_5_out, BITS___SIGNF[4]);
  not not_6 (not_6_out, BITS___SIGNF[5]);
  not not_7 (not_7_out, BITS___SIGNF[3]);
  and and_1 (and_1_out, not_1_out, BITS___SIGNF[1], not_7_out, not_2_out, not_8_out);
  not not_8 (not_8_out, BITS___SIGNF[5]);
  and and_2 (and_2_out, not_3_out, BITS___SIGNF[2], not_4_out, not_5_out, not_6_out);
  or or_1 (RD_RAM, and_1_out, and_2_out);
endmodule

module EN_PC (
  input  [5:0] BITS___SIGNF,
  output EN_PC
);

  wire and_1_out, and_2_out, and_3_out, not_1_out, not_2_out, not_3_out, not_4_out, not_5_out, not_6_out,
       not_7_out, not_8_out, not_9_out, not_10_out, not_11_out;

  not not_1 (not_1_out, BITS___SIGNF[3]);
  not not_2 (not_2_out, BITS___SIGNF[4]);
  not not_3 (not_3_out, BITS___SIGNF[5]);
  not not_4 (not_4_out, BITS___SIGNF[1]);
  not not_5 (not_5_out, BITS___SIGNF[2]);
  not not_6 (not_6_out, BITS___SIGNF[4]);
  not not_7 (not_7_out, BITS___SIGNF[5]);
  not not_8 (not_8_out, BITS___SIGNF[0]);
  not not_9 (not_9_out, BITS___SIGNF[2]);
  not not_10 (not_10_out, BITS___SIGNF[4]);
  not not_11 (not_11_out, BITS___SIGNF[5]);
  and and_1 (and_1_out, not_1_out, not_2_out, not_3_out);
  and and_2 (and_2_out, not_4_out, not_5_out, not_6_out, not_7_out);
  and and_3 (and_3_out, not_8_out, not_9_out, not_10_out, not_11_out);
  or or_1 (EN_PC, and_1_out, and_2_out, and_3_out);
endmodule

module WR_ACC (
  input  [5:0] BITS___SIGNF,
  output WR_ACC
);

  wire and_1_out, and_2_out, and_3_out, not_1_out, not_2_out, not_3_out, not_4_out, not_5_out, not_6_out,
       not_7_out, not_8_out, not_9_out, not_10_out;

  not not_1 (not_1_out, BITS___SIGNF[3]);
  not not_2 (not_2_out, BITS___SIGNF[4]);
  not not_3 (not_3_out, BITS___SIGNF[5]);
  not not_4 (not_4_out, BITS___SIGNF[3]);
  not not_5 (not_5_out, BITS___SIGNF[4]);
  not not_6 (not_6_out, BITS___SIGNF[5]);
  not not_7 (not_7_out, BITS___SIGNF[1]);
  not not_8 (not_8_out, BITS___SIGNF[2]);
  not not_9 (not_9_out, BITS___SIGNF[4]);
  not not_10 (not_10_out, BITS___SIGNF[5]);
  and and_1 (and_1_out, BITS___SIGNF[1], not_1_out, not_2_out, not_3_out);
  and and_2 (and_2_out, BITS___SIGNF[2], not_4_out, not_5_out, not_6_out);
  and and_3 (and_3_out, BITS___SIGNF[0], not_7_out, not_8_out, BITS___SIGNF[3], not_9_out, not_10_out);
  or or_1 (WR_ACC, and_1_out, and_2_out, and_3_out);
endmodule

module SEL_OP1 (
  input  [5:0] BITS___SIGNF,
  output [1:0] SEL_OP1
);

  wire and_1_out, and_2_out, not_1_out, not_2_out, not_3_out, not_4_out, not_5_out, not_6_out, not_7_out,
       not_8_out, not_9_out, not_10_out, not_11_out, not_12_out, not_13_out;

  not not_1 (not_1_out, BITS___SIGNF[0]);
  not not_2 (not_2_out, BITS___SIGNF[2]);
  not not_3 (not_3_out, BITS___SIGNF[3]);
  not not_4 (not_4_out, BITS___SIGNF[4]);
  not not_5 (not_5_out, BITS___SIGNF[5]);
  not not_6 (not_6_out, BITS___SIGNF[1]);
  not not_7 (not_7_out, BITS___SIGNF[2]);
  not not_8 (not_8_out, BITS___SIGNF[4]);
  not not_9 (not_9_out, BITS___SIGNF[5]);
  not not_10 (not_10_out, BITS___SIGNF[2]);
  not not_11 (not_11_out, BITS___SIGNF[3]);
  not not_12 (not_12_out, BITS___SIGNF[4]);
  not not_13 (not_13_out, BITS___SIGNF[5]);
  and and_1 (and_1_out, not_1_out, BITS___SIGNF[1], not_2_out, not_3_out, not_4_out, not_5_out);
  and and_2 (and_2_out, BITS___SIGNF[0], not_6_out, not_7_out, BITS___SIGNF[3], not_8_out, not_9_out);
  and and_3 (SEL_OP1[0], BITS___SIGNF[0], BITS___SIGNF[1], not_10_out, not_11_out, not_12_out, not_13_out);
  or or_1 (SEL_OP1[1], and_1_out, and_2_out);
endmodule

module SEL_OP2 (
  input  [5:0] BITS___SIGNF,
  output SEL_OP2
);

  wire not_1_out, not_2_out, not_3_out, not_4_out;

  not not_1 (not_1_out, BITS___SIGNF[0]);
  not not_2 (not_2_out, BITS___SIGNF[3]);
  not not_3 (not_3_out, BITS___SIGNF[4]);
  not not_4 (not_4_out, BITS___SIGNF[5]);
  and and_1 (SEL_OP2, not_1_out, BITS___SIGNF[2], not_2_out, not_3_out, not_4_out);
endmodule

module SEL_ULA (
  input  [5:0] BITS___SIGNF,
  output SEL_ULA
);

  wire not_1_out, not_2_out, not_3_out;

  not not_1 (not_1_out, BITS___SIGNF[3]);
  not not_2 (not_2_out, BITS___SIGNF[4]);
  not not_3 (not_3_out, BITS___SIGNF[5]);
  and and_1 (SEL_ULA, BITS___SIGNF[1], BITS___SIGNF[2], not_1_out, not_2_out, not_3_out);
endmodule

module EN_TEC (
  input  [5:0] BITS___SIGNF,
  output EN_TEC
);

  wire not_1_out, not_2_out, not_3_out, not_4_out;

  not not_1 (not_1_out, BITS___SIGNF[1]);
  not not_2 (not_2_out, BITS___SIGNF[2]);
  not not_3 (not_3_out, BITS___SIGNF[4]);
  not not_4 (not_4_out, BITS___SIGNF[5]);
  and and_1 (EN_TEC, BITS___SIGNF[0], not_1_out, not_2_out, BITS___SIGNF[3], not_3_out, not_4_out);
endmodule

module EN_MON (
  input  [5:0] BITS___SIGNF,
  output EN_MON
);

  wire not_1_out, not_2_out, not_3_out, not_4_out;

  not not_1 (not_1_out, BITS___SIGNF[0]);
  not not_2 (not_2_out, BITS___SIGNF[2]);
  not not_3 (not_3_out, BITS___SIGNF[4]);
  not not_4 (not_4_out, BITS___SIGNF[5]);
  and and_1 (EN_MON, not_1_out, BITS___SIGNF[1], not_2_out, BITS___SIGNF[3], not_3_out, not_4_out);
endmodule

module SEL_JUMP (
  input  [5:0] BITS___SIGNF,
  output SEL_JUMP
);

  wire not_1_out, not_2_out, not_3_out, not_4_out, not_5_out;

  not not_1 (not_1_out, BITS___SIGNF[0]);
  not not_2 (not_2_out, BITS___SIGNF[1]);
  not not_3 (not_3_out, BITS___SIGNF[2]);
  not not_4 (not_4_out, BITS___SIGNF[4]);
  not not_5 (not_5_out, BITS___SIGNF[5]);
  and and_1 (SEL_JUMP, not_1_out, not_2_out, not_3_out, BITS___SIGNF[3], not_4_out, not_5_out);
endmodule
